// Logisim project CPU.circ as structural Verilog: 1 circuit, main circuit CPU
module CPU (
  input  Fetch,
  output out_2,
  output [9:0] out_3
);

  wire clock_1_out;
  wire [9:0] n10bitincrementer_1_s;

  Clock clock_1 (.out(clock_1_out));
  _10BitRegister PC (.clk(clock_1_out), .W_Enable(Fetch), .I(n10bitincrementer_1_s), .Q(out_3));
  _10BitIncrementer u_10bitincrementer_1 (.I(out_3), .S(n10bitincrementer_1_s), .Overflow(out_2));

  // Notes on the sheet:
  //   out_3: pull=down
  //   Fetch: pull=down
endmodule
