// Logisim project Terminator.circ as structural Verilog: 1 circuit, main circuit Terminator
module Terminator (
  input  clk,
  input  Decode,
  input  Halt_Instruction,
  input  Stack_Overflow,
  input  Instruction_End,
  input  PC_Overflow,
  output Halted
);

  wire and_1_out, and_2_out, Delay_q, Halted_q, or_1_out, PCOverflowed_q, Started_q;

  RisingEdgeTriggeredDFlipFlop Started (.D(Decode), .clk(clk), .Q(Started_q), .W_Enable(Decode));
  RisingEdgeTriggeredDFlipFlop PCOverflowed (.D(PC_Overflow), .clk(clk), .Q(PCOverflowed_q), .W_Enable(PC_Overflow));
  and and_1 (and_1_out, Started_q, Halt_Instruction);
  and and_2 (and_2_out, Instruction_End, PCOverflowed_q);
  FallingEdgeTriggeredDFlipFlop Delay (.D(1'b1), .C(and_2_out), .Q(Delay_q));
  or or_1 (or_1_out, and_1_out, Stack_Overflow, Delay_q);
  RisingEdgeTriggeredDFlipFlop u_Halted (.D(or_1_out), .clk(or_1_out), .Q(Halted_q), .W_Enable(or_1_out));
  or or_2 (Halted, Halted_q, or_1_out);

  // Notes on the sheet:
  //   Decode: pull=down
  //   Stack_Overflow: pull=down
  //   Halt_Instruction: pull=down
  //   PC_Overflow: pull=down
  //   clk: pull=down
  //   Halted: pull=down
  //   Instruction_End: pull=down
endmodule
