// Logisim project FallingEdgeTriggeredDFlipFlop.circ as structural Verilog: 1 circuit, main circuit FallingEdgeTriggeredDFlipFlop
module FallingEdgeTriggeredDFlipFlop (
  input  D,
  input  C,
  output Q
);

  wire dlatch_1_q, not_1_out;

  DLatch dlatch_1 (.D(D), .C(C), .Q(dlatch_1_q));
  not not_1 (not_1_out, C);
  DLatch dlatch_2 (.D(dlatch_1_q), .C(not_1_out), .Q(Q));
endmodule
