// Logisim project RisingEdgeTriggeredDFlipFlop.circ as structural Verilog: 1 circuit, main circuit RisingEdgeTriggeredDFlipFlop
module RisingEdgeTriggeredDFlipFlop (
  input  D,
  input  E,
  input  C,
  output Q
);

  wire dlatch_1_q, multiplexer_1_out, not_1_out;

  Multiplexer #(.enable("false")) multiplexer_1 (.in0(Q), .in1(D), .out(multiplexer_1_out), .sel(E));
  not not_1 (not_1_out, C);
  DLatch dlatch_1 (.D(multiplexer_1_out), .clk(not_1_out), .Q(dlatch_1_q));
  DLatch dlatch_2 (.D(dlatch_1_q), .clk(C), .Q(Q));

  // Notes on the sheet:
  //   D: pull=down
  //   C: pull=down
  //   E: pull=down
  //   Q: pull=down
endmodule
