// Logisim project Memory.circ as structural Verilog: 1 circuit, main circuit Memory
module Memory (
  input  [9:0] PC,
  input  [19:0] D,
  input  [9:0] A,
  input  reset,
  input  clk,
  input  WR_Select,
  output [19:0] Inst,
  output [19:0] D_2
);

  wire not_1_out, not_2_out;
  wire [9:0] MAR_q;

  not not_1 (not_1_out, WR_Select);
  not not_2 (not_2_out, clk);
  RAM #(.addrWidth(10), .dataWidth(20), .bus("separate")) ram_1 (
    .addr(A), .din(D), .data(D_2), .str(WR_Select), .clk(clk), .ld(not_1_out));  // open: sel, clr
  _10BitRegister MAR (.clk(not_2_out), .W_Enable(1'b1), .I(PC), .Q(MAR_q), .reset(reset));
  RAM #(.addrWidth(10), .dataWidth(20), .bus("separate")) ram_2 (
    .addr(MAR_q), .data(Inst), .ld(1'b1));  // open: din, str, sel, clk, clr

  // Notes on the sheet:
  //   WR_Select: pull=down
  //   clk: pull=down
  //   A: pull=down
  //   reset: pull=down
  //   D_2: pull=down
  //   Inst: pull=down
  //   PC: pull=down
  //   D: pull=down
  //   Data Memory
  //   Instruction Memory
endmodule
