// Logisim project 10BitRegister.circ as structural Verilog: 1 circuit, main circuit 10BitRegister
module _10BitRegister (
  input  [9:0] I,
  input  C,
  input  E,
  output [9:0] Q
);

  RisingEdgeTriggeredDFlipFlop risingedgetriggereddflipflop_1 (.D(I[9]), .clk(C), .Q(Q[9]), .W_Enable(E));
  RisingEdgeTriggeredDFlipFlop risingedgetriggereddflipflop_2 (.D(I[8]), .clk(C), .Q(Q[8]), .W_Enable(E));
  RisingEdgeTriggeredDFlipFlop risingedgetriggereddflipflop_3 (.D(I[7]), .clk(C), .Q(Q[7]), .W_Enable(E));
  RisingEdgeTriggeredDFlipFlop risingedgetriggereddflipflop_4 (.D(I[6]), .clk(C), .Q(Q[6]), .W_Enable(E));
  RisingEdgeTriggeredDFlipFlop risingedgetriggereddflipflop_5 (.D(I[5]), .clk(C), .Q(Q[5]), .W_Enable(E));
  RisingEdgeTriggeredDFlipFlop risingedgetriggereddflipflop_6 (.D(I[4]), .clk(C), .Q(Q[4]), .W_Enable(E));
  RisingEdgeTriggeredDFlipFlop risingedgetriggereddflipflop_7 (.D(I[3]), .clk(C), .Q(Q[3]), .W_Enable(E));
  RisingEdgeTriggeredDFlipFlop risingedgetriggereddflipflop_8 (.D(I[2]), .clk(C), .Q(Q[2]), .W_Enable(E));
  RisingEdgeTriggeredDFlipFlop risingedgetriggereddflipflop_9 (.D(I[1]), .clk(C), .Q(Q[1]), .W_Enable(E));
  RisingEdgeTriggeredDFlipFlop risingedgetriggereddflipflop_10 (.D(I[0]), .clk(C), .Q(Q[0]), .W_Enable(E));

  // Notes on the sheet:
  //   Q: pull=down
  //   C: pull=down
  //   I: pull=down
  //   E: pull=down
endmodule
