// Logisim project 20BitRegister.circ as structural Verilog: 1 circuit, main circuit 20BitRegister
module _20BitRegister (
  input  [19:0] I,
  input  C,
  input  E,
  output [19:0] Q
);

  RisingEdgeTriggeredDFlipFlop risingedgetriggereddflipflop_1 (.D(I[19]), .clk(C), .Q(Q[19]), .W_Enable(E));
  RisingEdgeTriggeredDFlipFlop risingedgetriggereddflipflop_2 (.D(I[18]), .clk(C), .Q(Q[18]), .W_Enable(E));
  RisingEdgeTriggeredDFlipFlop risingedgetriggereddflipflop_3 (.D(I[17]), .clk(C), .Q(Q[17]), .W_Enable(E));
  RisingEdgeTriggeredDFlipFlop risingedgetriggereddflipflop_4 (.D(I[16]), .clk(C), .Q(Q[16]), .W_Enable(E));
  RisingEdgeTriggeredDFlipFlop risingedgetriggereddflipflop_5 (.D(I[15]), .clk(C), .Q(Q[15]), .W_Enable(E));
  RisingEdgeTriggeredDFlipFlop risingedgetriggereddflipflop_6 (.D(I[14]), .clk(C), .Q(Q[14]), .W_Enable(E));
  RisingEdgeTriggeredDFlipFlop risingedgetriggereddflipflop_7 (.D(I[13]), .clk(C), .Q(Q[13]), .W_Enable(E));
  RisingEdgeTriggeredDFlipFlop risingedgetriggereddflipflop_8 (.D(I[12]), .clk(C), .Q(Q[12]), .W_Enable(E));
  RisingEdgeTriggeredDFlipFlop risingedgetriggereddflipflop_9 (.D(I[11]), .clk(C), .Q(Q[11]), .W_Enable(E));
  RisingEdgeTriggeredDFlipFlop risingedgetriggereddflipflop_10 (.D(I[10]), .clk(C), .Q(Q[10]), .W_Enable(E));
  RisingEdgeTriggeredDFlipFlop risingedgetriggereddflipflop_11 (.D(I[9]), .clk(C), .Q(Q[9]), .W_Enable(E));
  RisingEdgeTriggeredDFlipFlop risingedgetriggereddflipflop_12 (.D(I[8]), .clk(C), .Q(Q[8]), .W_Enable(E));
  RisingEdgeTriggeredDFlipFlop risingedgetriggereddflipflop_13 (.D(I[7]), .clk(C), .Q(Q[7]), .W_Enable(E));
  RisingEdgeTriggeredDFlipFlop risingedgetriggereddflipflop_14 (.D(I[6]), .clk(C), .Q(Q[6]), .W_Enable(E));
  RisingEdgeTriggeredDFlipFlop risingedgetriggereddflipflop_15 (.D(I[5]), .clk(C), .Q(Q[5]), .W_Enable(E));
  RisingEdgeTriggeredDFlipFlop risingedgetriggereddflipflop_16 (.D(I[4]), .clk(C), .Q(Q[4]), .W_Enable(E));
  RisingEdgeTriggeredDFlipFlop risingedgetriggereddflipflop_17 (.D(I[3]), .clk(C), .Q(Q[3]), .W_Enable(E));
  RisingEdgeTriggeredDFlipFlop risingedgetriggereddflipflop_18 (.D(I[2]), .clk(C), .Q(Q[2]), .W_Enable(E));
  RisingEdgeTriggeredDFlipFlop risingedgetriggereddflipflop_19 (.D(I[1]), .clk(C), .Q(Q[1]), .W_Enable(E));
  RisingEdgeTriggeredDFlipFlop risingedgetriggereddflipflop_20 (.D(I[0]), .clk(C), .Q(Q[0]), .W_Enable(E));

  // Notes on the sheet:
  //   C: pull=down
  //   Q: pull=down
  //   E: pull=down
  //   I: pull=down
endmodule
